# Fritzing sketch Lockery (saved by Fritzing 0.9.5d)
breadboards: 2

parts:
  Nano1 = Arduino Nano v2.3
  LED2 = LED - 3mm [color="Red (633nm)" package="3 mm [THT]"]
  R1 = Resistor [tolerance=±5% resistance=500 package="2010 [SMD]"]
  Part1 = RFID-RC522-v2
  S1 = Pushbutton [package="[THT]"]
  R2 = Resistor [tolerance=±5% resistance=1k package="2010 [SMD]"]
  U1 = BATTERY-2 [package=battery-aa]
  Raspberry_Pi_1 = Raspberry Pi 3 [part_number=RPI-3-V1.2]
  Part2 = RFID-RC522-v2
  S2 = Momentary Switch [package=ksa_sealed_tac_switch]
  S3 = Momentary Switch [package=ksa_sealed_tac_switch]
  S4 = Momentary Switch [package=ksa_sealed_tac_switch]
  R3 = Resistor [tolerance=±5% resistance=1k package="2010 [SMD]"]
  R4 = Resistor [tolerance=±5% resistance=1k package="2010 [SMD]"]
  R5 = Resistor [tolerance=±5% resistance=1k package="2010 [SMD]"]
  J1 = Piezo Speaker
  VCC1 = Battery block 9V
  LED3 = LED - 3mm [color="Red (633nm)" package="3 mm [THT]"]
  LED4 = LED - 3mm [color="Red (633nm)" package="3 mm [THT]"]
  LED5 = LED - 3mm [color="Red (633nm)" package="3 mm [THT]"]
  R6 = Resistor [tolerance=±5% resistance=500 package=THT]
  R7 = Resistor [tolerance=±5% resistance=500 package=THT]
  J2 = Basic Servo
  Part3 = sensor_biometrico

nets:
  GND: Nano1.GND, LED2.cathode, Part1.GND, S1.Pin_1, S1.Pin_2, U1.-1, Part3.GND
  N1: Nano1.D4, R2.Pin_0
  N2: Nano1.D6, Part3.TX
  N3: Nano1.D7, Part3.RX
  3V3: Nano1.3V3, Part1.3.3V
  N4: Nano1.A6, Part1.SDA
  N5: Nano1.A5, Part1.SCK
  N6: Nano1.A4, Part1.MOSI
  N7: Nano1.A3, Part1.MISO
  N8: Nano1.A2, Part1.IRQ
  N9: Nano1.A1, LED2.anode, R1.Pin_0, R1.Pin_1
  +5V: Nano1.+5V, R2.Pin_1, U1.+1, Part3.VCC
  N10: S1.Pin_3, S1.Pin_4
  3V3_2: Raspberry_Pi_1.3v3, Part2.3.3V
  GND_2: Raspberry_Pi_1.GND, Part2.RST, S2.3, S2.4, S3.3, S3.4, S4.3, S4.4, J1.pin1, VCC1.-, LED3.anode, LED4.anode, J2.gnd
  N11: Raspberry_Pi_1.GPIO17, J1.pin2, VCC1.+, LED5.anode, J2.vcc
  N12: Raspberry_Pi_1.GPIO5, Part2.SDA
  N13: Raspberry_Pi_1.GPIO6, Part2.SCK
  N14: Raspberry_Pi_1.GPIO13, Part2.MOSI
  N15: Raspberry_Pi_1.GPIO19, Part2.MISO
  N16: Raspberry_Pi_1.GPIO26, Part2.IRQ
  N17: Raspberry_Pi_1.GPIO20, LED5.cathode
  N18: Raspberry_Pi_1.GPIO7, R7.Pin_1
  N19: S2.1, S2.2, R4.Pin_0
  N20: S3.1, S3.2, R5.Pin_0
  N21: S4.1, S4.2, R3.Pin_0
  N22: LED3.cathode, R6.Pin_0
  N23: LED4.cathode, R7.Pin_0

notes:
  Servo to lock and unlock the cylinder-lock
  Battery to power up the whole system (smart cylinder)
  Beeper to get feedback about the user actions
  Led lights to give visual feedback about the user actions + sanity / liveness checks
  NFC Reader to read the key NFC ID
  Push buttons to enable:
  Paring a key
  Enable / Disable WIFI
  RESET System
  Battery to power up the whole system (smart key)
  Biometric Fingerprint reader - to read the user fingerprint into a hash
  NFC Transmitter to send the key NFC ID to Smart Cylinder
  Led light to give a feedback about the lock / unlock of the last used cylinder
  Push button to activate the fingerprint reader (save energy when the fingerprint reader is not in use)

custom parts:
  RFID-RC522-v2: A simple China made RFID-RC522 Reader; do check the pin labels, as this is a MFRC522 based clone.
  sensor_biometrico: Adafruit Optical Fingerprint Sensor
